# Fritzing sketch scheme (saved by Fritzing 1.0.5)
breadboards: 1

parts:
  Capacitive_Soil_Moisture_Sensor1 = DFRobot Capacitive Soil Moisture Sensor V1.0 [part_number=SEN0193]
  A1 = Esp32-c3 super mini
  M1 = TP4056 Module [part_number=HW-107]
  U1 = LIPO-2000mAh [package=lipo-2000]
  R1 = Resistor [tolerance=±5% resistance=100000 package="0603 [SMD]"]
  R2 = Resistor [tolerance=±5% resistance=100000 package="0603 [SMD]"]

nets:
  N1: Capacitive_Soil_Moisture_Sensor1.A, A1.Pin_9
  N2: Capacitive_Soil_Moisture_Sensor1.VCC, A1.Pin_14
  N3: Capacitive_Soil_Moisture_Sensor1.GND, A1.Pin_15, M1.OUT-#1, R2.Pin_0
  N4: A1.Pin_10, R1.Pin_0, R2.Pin_1
  N5: A1.Pin_16, M1.OUT-#4
  N6: M1.BAT-, U1.-
  N7: M1.BAT+, U1.+

custom parts:
  DFRobot Capacitive Soil Moisture Sensor V1.0: DFRobot Capacitive Soil Moisture Sensor V1.0 This product measures soil moisture levels by capacitive sensing, rather than resistive sensing like other types of moisture sensor. It is made of a corrosion resistant material giving it a long service life. Insert it into soil and impress your friends with the real-time soil moisture data! The product includes an on-board voltage regulator which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
  Esp32-c3 super mini: ESP32-C3 Development Board ESP32 SuperMini Development Board ESP32 Development Board WiFi Bluetooth.
  TP4056 Module: TP4056 Lithium Battery Charge Management Module Links: TP4056 website
